# Fritzing sketch 33 (saved by Fritzing 0.9.3b)
breadboards: 1

parts:
  T1 = LM35 Temperature Sensor [package="TO92 [THT]"]
  Part1 = Arduino Uno (Rev3)
  J1 = Basic Servo
  SG1 = Buzzer 12mm [package=buzzer-12mm-ns-kit]

nets:
  5V: T1.+Vs, Part1.5V, J1.vcc
  N1: T1.Vout, Part1.A1
  GND: T1.GND, Part1.GND, J1.gnd, SG1.2
  N2: Part1.D4, SG1.1
  N3: Part1.D5_PWM, J1.pulse
